# Fritzing sketch unijoysticle (saved by Fritzing 0.9.2b)
circuit board: 10.4547cm x 6.89937cm
breadboards: 1

parts:
  U1 = NodeMCU V1.0 [part_number="NodeMCU Amica"]
  4066 = DIP - 14 pins [chip_label=4066 part_number=SN74HC4066 package="DIP (Dual Inline) [THT]"]
  4066_2 = DIP - 14 pins [chip_label=4066 part_number=SN74HC4066 package="DIP (Dual Inline) [THT]"]
  X1 = DB9 Connector [package=db9]
  X2 = DB9 Connector [package=db9]
  4066_3 = DIP - 14 pins [chip_label=4066 part_number=SN74HC4066 package="DIP (Dual Inline) [THT]"]

nets:
  N1: U1.D0, 4066_2.1C
  N2: U1.D1, 4066_2.2C
  N3: U1.D2, 4066_2.3C
  N4: U1.D3, 4066_2.4C
  N5: U1.D4, 4066_3.1C
  VCC: U1.3V3, 4066.Vcc, 4066_2.Vcc, 4066_3.Vcc
  GND: U1.GND, 4066.GND, 4066_2.GND, 4066_3.GND
  N6: U1.D5, 4066.1C
  N7: U1.D6, 4066.2C
  N8: U1.D7, 4066.3C
  N9: U1.D8, 4066.4C
  N10: U1.RX, 4066_3.2C
  N11: 4066.1A, X2.1
  N12: 4066.1B, 4066.2B, 4066.3B, 4066.4B, X2.8, 4066_3.1B, 4066_3.2B
  N13: 4066.2A, X2.2
  N14: 4066.3A, X2.3
  N15: 4066.4A, X2.4
  N16: 4066_2.1A, X1.1
  N17: 4066_2.1B, 4066_2.2B, 4066_2.3B, 4066_2.4B, X1.8
  N18: 4066_2.2A, X1.2
  N19: 4066_2.3A, X1.3
  N20: 4066_2.4A, X1.4
  N21: X1.6, 4066_3.1A
  N22: X2.6, 4066_3.2A

notes:
  UniJoystiCle v0.2
  Joy Port #1
  Joy Port #2
  Control Port #1
  Control Port #2

custom parts:
  NodeMCU V1.0: ESP9266 based NodeMCU
  DIP - 14 pins: Quadruple bilateral analog switch
  DB9 Connector: DB9 Connector Standard DB9 (D-Sub 9) serial connector. Can be used for CAN bus as well as RS485 and RS232. Footprint production proven. Spark Fun Electronics SKU : PRT-00429
